# Fritzing sketch servo (saved by Fritzing 0.9.2b)
breadboards: 1

parts:
  Part3 = Arduino Uno (Rev3)
  Part4 = LIDAR-Lite

nets:
  GND: Part3.A4/SDA, Part3.GND, Part4.SDA, Part4.GND
  N1: Part3.A5/SCL, Part4.SCL
  5V: Part3.5V, Part4.5V

custom parts:
  LIDAR-Lite: PulsedLight LIDAR-Lite Sensor
